# Fritzing sketch breadboardCircuit (saved by Fritzing 0.9.3b)
breadboards: 2

parts:
  元件1 = Arduino Uno (Rev3)
  Q1 = Basic FET N-Channel [package="TO220 [THT]"]
  Q2 = Basic FET N-Channel [package="TO220 [THT]"]
  U1 = Vibration Motor- ROB-08449 [package=vibe-motor-10mm]
  U2 = Vibration Motor- ROB-08449 [package=vibe-motor-10mm]
  VCC1 = Battery block 9V
  HC-SR04_Sensor_1 = HC-SR04 Ultrasonic Distance Sensor
  HC-SR04_Sensor_2 = HC-SR04 Ultrasonic Distance Sensor

nets:
  N1: 元件1.D8, Q1.gate
  N2: 元件1.D9_PWM, HC-SR04_Sensor_1.ECHO
  N3: 元件1.D10_PWM/SS, HC-SR04_Sensor_1.TRIG
  N4: 元件1.D5_PWM, Q2.gate
  N5: 元件1.D6_PWM, HC-SR04_Sensor_2.ECHO
  N6: 元件1.D7, HC-SR04_Sensor_2.TRIG
  5V: 元件1.5V, U1.-, U2.-, HC-SR04_Sensor_1.VCC, HC-SR04_Sensor_2.VCC
  GND: 元件1.GND, Q1.source, Q2.source, VCC1.-, HC-SR04_Sensor_1.GND, HC-SR04_Sensor_2.GND
  N7: 元件1.VIN, VCC1.+
  N8: Q1.drain, U1.+
  N9: Q2.drain, U2.+

notes:
  Black - GND
  Red - 5V
  Pink - 9V
  Blue - to Arduino GPIO
  Purple - to Vibration Motor
  <--- Vibration motor
  Yiru Liu
  9V Battery

custom parts:
  HC-SR04 Ultrasonic Distance Sensor: The HC-SR04 is an ultrasonic distance sensor. It is capable of providing measurement for ranges of 2cm to 400cm. The module operates at 5V.
