# Fritzing sketch breadboardCircuit (saved by Fritzing 0.9.4)
breadboards: 2

parts:
  元件1 = Arduino Uno (Rev3)
  U1 = Vibration Motor- ROB-08449 [package=vibe-motor-10mm]
  U2 = Vibration Motor- ROB-08449 [package=vibe-motor-10mm]
  VCC1 = Battery block 9V
  HC-SR04_Sensor_1 = HC-SR04 Ultrasonic Distance Sensor
  HC-SR04_Sensor_2 = HC-SR04 Ultrasonic Distance Sensor
  Q1 = NPN-Transistor [part_number=S8050 package="TO92 [THT]"]
  R1 = Resistor [tolerance=±1% resistance=1.5k package=THT]
  Q2 = NPN-Transistor [part_number=S8050 package="TO92 [THT]"]
  R2 = Resistor [tolerance=±1% resistance=1.5k package=THT]
  D2 = Rectifier Diode [part_number=1N4007 package="300 mil [THT]"]
  D1 = Rectifier Diode [part_number=1N4007 package="300 mil [THT]"]
  D3 = Rectifier Diode [part_number=1N4007 package="300 mil [THT]"]

nets:
  N1: 元件1.D8, R1.Pin_0
  N2: 元件1.D9_PWM, HC-SR04_Sensor_1.ECHO
  N3: 元件1.D10_PWM/SS, HC-SR04_Sensor_1.TRIG
  N4: 元件1.D5_PWM, R2.Pin_0
  N5: 元件1.D6_PWM, HC-SR04_Sensor_2.ECHO
  N6: 元件1.D7, HC-SR04_Sensor_2.TRIG
  3.3V: 元件1.3V3, U1.-, U2.-, D2.cathode, D1.cathode
  5V: 元件1.5V, HC-SR04_Sensor_1.VCC, HC-SR04_Sensor_2.VCC
  GND: 元件1.GND, VCC1.-, HC-SR04_Sensor_1.GND, HC-SR04_Sensor_2.GND, Q1.E, Q2.E
  N7: 元件1.VIN, D3.cathode
  N8: U1.+, Q1.C, D1.anode
  N9: U2.+, Q2.C, D2.anode
  N10: VCC1.+, D3.anode
  N11: Q1.B, R1.Pin_1
  N12: Q2.B, R2.Pin_1

notes:
  Black - GND
  Orange - 3.3V
  Red - 5V
  Pink - 9V
  Blue - to Arduino GPIO
  Purple - to Vibration Motor
  <--- Vibration motor
  Yiru Liu
  9V Battery

custom parts:
  HC-SR04 Ultrasonic Distance Sensor: The HC-SR04 is an ultrasonic distance sensor. It is capable of providing measurement for ranges of 2cm to 400cm. The module operates at 5V.
